# Fritzing sketch pixel-flash-v94 (saved by Fritzing 1.0.3b)
breadboards: 1

parts:
  U1 = CH32V003F4U6 [part_number=CH32V003F4U6 package=QFN20]

nets:
  N1: U1.VSS, U1.EPAD
  N2: U1.VDD, U1.PD1

notes:
  SWDIO
  5V
  GND

custom parts:
  CH32V003F4U6: WCH CH32V003F4U6 RISC-V MCU, QFN20 3x3 mm / 0.4 mm pitch, 3.3-5 V, 10-bit ADC (6 channels + 2) and one internal OPA, 18 I/O. Pin compatible with CH32V002F4U6 (12-bit ADC, no OPA) - drop-in. Exposed pad EPAD (internally VSS) - route to GND.
