# Fritzing sketch pixel-pcb-v90 (saved by Fritzing 1.0.3b)
circuit board: 2.5cm x 2.5cm
breadboards: 1

parts:
  L1 = NFC Coil [part_number=NFC-Coil-20-6T package=PCB]
  C2 = Capacitor 0603 [capacitance="100 nF" voltage=16V package="[SMD] 0603"]
  C1 = Capacitor 0603 [capacitance="100 nF" voltage=16V package="[SMD] 0603"]
  R1 = R0603 [tolerance=±5% resistance=220 power=1/10W]
  LED2 = WS2812B-1010 [part_number=WS2812B-1010 package="WS2812B-1010 (1.0x1.0mm)"]
  U1 = CH32V003F4U6 [part_number=CH32V003F4U6 package=QFN20]
  D3 = BAS70BRW [part_number=BAS70BRW package="SOT-363 (SC-70-6)"]
  J1 = 1.0mm 3P vertical SMD socket (SH1.0-3P-LT) [part_number=SH1.0-3P-LT]
  J2 = 1.0mm 3P vertical SMD socket (SH1.0-3P-LT) [part_number=SH1.0-3P-LT]
  D4 = Schottky Diode [capacitance="100 nF" voltage=16V part_number=1N5819 package="SOD323[SMD]"]
  R2 = R0603 [capacitance="100 nF" voltage=16V tolerance=±1% power=1/10W resistance=4.7k]
  R3 = R0603 [capacitance="100 nF" voltage=16V tolerance=±1% power=1/10W resistance=4.7k]
  R4 = R0603 [capacitance="100 nF" voltage=16V tolerance=±1% power=1/10W resistance=4.7k]

nets (from the pcb view):
  N1: L1.inner, D3.AC1
  N2: L1.outer, D3.AC2
  VDD: C2.1, LED2.VDD, U1.VDD, J1.1, J2.1
  GND: C2.2, C1.2, LED2.GND, U1.VSS, U1.EPAD, D3.A1, D3.A2, J1.2, J2.2, D4.anode, R2.connector1, R3.connector1, R4.connector1
  N3: C1.1, R1.connector1, U1.PD6, D4.cathode, R2.connector0, R3.connector0, R4.connector0
  N4: R1.connector0, D3.C2, D3.C1
  N5: LED2.DI, U1.PC6
  N6: U1.PC1, J1.3
  N7: U1.PD2, J2.3

notes:
  花石箓
  NFC-Pixel
  v0.1.1
  图例：
  GND
  5V
  DATA_IN
  DATA_OUT
  LED_DIN
  RC
  BR+
  COIL_A
  COIL_B
  DATA_IN_C
  DATA_OUT_C

custom parts:
  NFC Coil: 13.56 MHz NFC sensing coil (PCB spiral, 20 mm OD, 6 turns)
  Capacitor 0603: A generic capacitor
  WS2812B-1010: WS2812B-1010 addressable RGB LED, 1.0x1.0x0.8 mm, integrated driver, 4 bottom pads on a 0.40 mm grid.
  CH32V003F4U6: WCH CH32V003F4U6 RISC-V MCU, QFN20 3x3 mm / 0.4 mm pitch, 3.3-5 V, 10-bit ADC (6 channels + 2) and one internal OPA, 18 I/O. Pin compatible with CH32V002F4U6 (12-bit ADC, no OPA) - drop-in. Exposed pad EPAD (internally VSS) - route to GND.
  BAS70BRW: Diodes BAS70BRW-7-F: 4 x 70 V Schottky diodes in SOT-363 (SC-70-6), wired as two series pairs with all six nodes available (A1/AC1/C1 and A2/AC2/C2). Suitable as a 4-diode bridge for low-current envelope detection.
  1.0mm 3P vertical SMD socket (SH1.0-3P-LT): SH1.0 1mm 3P vertical SMD socket (SH1.0-3P-LT), board side. Breadboard view = green adapter board with 3 header pins on the 2.54mm grid (the SMD socket itself cannot plug into a breadboard). Pads follow the manufacturer drawing.
  Schottky Diode: A standard schottky barrier rectifier diode
