# Fritzing sketch ws2812b-4x4-test (saved by Fritzing 1.0.3b)
breadboards: 2

parts:
  U1 = ESP32-S3-DevKitC-1 [part_number=ESP32-S3-DevKitC-1]
  R1 = Resistor [tolerance=±5% power=0.25W resistance=330 package=THT]
  LED1 = WS2812B-5050-4x4 [part_number=WS2812B-5050-4x4 package="WS2812B-5050 4x4 Module (30x30mm)"]

nets:
  N1: U1.GND, LED1.GND#0
  3V3: U1.3V3, LED1.VCC
  N2: U1.15, R1.Pin_0
  N3: R1.Pin_1, LED1.DIN

custom parts:
  ESP32-S3-DevKitC-1: ESP32-S3-DevKitC-1 development board, 63.5x28mm, 44 pins, based on ESP32-S3-WROOM-1 (WiFi + BLE).
  WS2812B-5050-4x4: 4x4 WS2812B-5050 RGB matrix module, black board ~30x30mm, LEDs spread evenly (pitch 7.5mm), 12 bypass caps, 4 mount holes. 8 pins: bottom GND/VCC/DIN/GND, top GND/VCC/DOUT/GND (2.54mm). LED scan order serpentine from bottom-right (1..16) - verify against the real module silkscreen.
