# Fritzing sketch ws2812b-single-test (saved by Fritzing 1.0.3b)
breadboards: 2

parts:
  LED1 = WS2812B-5050 [part_number=WS2812B-5050 package="WS2812B-5050 (5.0x5.0mm)"]
  U1 = ESP32-S3-DevKitC-1 [part_number=ESP32-S3-DevKitC-1]
  R1 = Resistor [tolerance=±5% power=0.25W resistance=330 package=THT]

nets:
  N1: LED1.VDD, U1.3V3#1
  N2: LED1.DI, R1.Pin_1
  N3: LED1.GND, U1.GND#39
  N4: U1.15, R1.Pin_0

custom parts:
  WS2812B-5050: WS2812B-5050 addressable RGB LED, 5.0x5.0 mm, integrated driver.
  ESP32-S3-DevKitC-1: ESP32-S3-DevKitC-1 development board, 63.5x28mm, 44 pins, based on ESP32-S3-WROOM-1 (WiFi + BLE).
