# Fritzing sketch single-channel (saved by Fritzing 1.0.3b)
breadboards: 2

parts:
  U3 = CD74HC4067 [part_number=CD74HC4067]
  D1 = BAT54S [part_number=BAT54S package=SOT23-3]
  D2 = BAT54S [part_number=BAT54S package=SOT23-3]
  L1 = NFC Coil [part_number=NFC-Coil-20-6T package=PCB]
  U2 = TS3A44159PWR [part_number=TS3A44159PWR package=TSSOP-16]
  R1 = Resistor [tolerance=±1% resistance=220 power=0.25W package="0603 [SMD]"]
  C1 = Ceramic Capacitor [capacitance=100nF voltage=35V package="0603 [SMD, multilayer]"]

nets:
  N1: U3.C0, U2.NO1
  ESP32-S3-DevKitC-1 IO1: U3.SIG
  ESP32-S3-DevKitC-1 IO4: U3.S0
  ESP32-S3-DevKitC-1 IO5: U3.S1
  ESP32-S3-DevKitC-1 IO6: U3.S2
  ESP32-S3-DevKitC-1 IO7: U3.S3
  ESP32-S3-DevKitC-1 GND: U3.EN, U3.GND, D1.A1, D2.A1, U2.GND, U2.NC1, C1.0
  ESP32-S3-DevKitC-1 3V3: U3.VCC, U2.VCC
  N2: D1.K2, D2.K2, R1.Pin_0
  N3: D1.node, L1.inner
  N4: D2.node, L1.outer
  ESP32-S3-DevKitC-1 IO2: U2.IN3-4, U2.IN1-2
  N5: U2.COM1, R1.Pin_1, C1.1

custom parts:
  CD74HC4067: 16-channel analog/digital multiplexer (CD74HC4067), terminals C0-C15 / SIG / S0-S3 / EN / VCC / GND.
  BAT54S: Dual series Schottky diode, SOT-23. Two diodes: pin1->pin3->pin2.
  NFC Coil: 13.56 MHz NFC sensing coil (PCB spiral, 20 mm OD, 6 turns)
  TS3A44159PWR: Quad SPDT / dual DPDT bidirectional analog switch, 1.65-4.3 V, TSSOP-16 (PW).
